# Fritzing sketch Bina - 3 (saved by Fritzing 0.8.7b)
breadboards: 1

parts:
  DTMF-IC1 = MT8870 [package="DIP (Dual Inline) [THT]"]
  R1 = Resistor [tolerance=±5% resistance=56k package=THT]
  R2 = Resistor [tolerance=±5% resistance=56k package=THT]
  R3 = Resistor [tolerance=±5% resistance=47k package=THT]
  R4 = Resistor [tolerance=±5% resistance=68k package=THT]
  D1 = Zener Diode [part_number=1N4732A breakdown_voltage=5.6V package="300 mil [THT]"]
  D2 = Zener Diode [part_number=1N4732A breakdown_voltage=5.6V package="300 mil [THT]"]
  C1 = Ceramic Capacitor [capacitance=100nF voltage=500V package="100 mil [THT, multilayer]"]
  C2 = Ceramic Capacitor [capacitance=100nF voltage=500V package="100 mil [THT, multilayer]"]
  R5 = Resistor [tolerance=±5% resistance=56k package=THT]
  R6 = Resistor [tolerance=±5% resistance=56k package=THT]
  J1 = RJ11 Jack [package=rj11-6]
  R7 = Resistor [tolerance=±5% resistance=150k package=THT]
  XTAL2 = Crystal [package=THT]
  Componente1 = Arduino Uno (Rev3)
  R8 = Resistor [tolerance=±5% resistance=330k package=THT]
  C3 = Ceramic Capacitor [capacitance=100nF package="100 mil [THT, multilayer]"]
  D3 = Rectifier Diode [part_number=1N4007 package="300 mil [THT]"]
  D4 = Rectifier Diode [part_number=1N4007 package="300 mil [THT]"]
  D5 = Rectifier Diode [part_number=1N4007 package="300 mil [THT]"]
  D6 = Rectifier Diode [part_number=1N4007 package="300 mil [THT]"]
  U2 = Transformer [package=transformer]

nets:
  + audio: DTMF-IC1.IN_+, R3.Pin_1, U2.4
  - audio: DTMF-IC1.IN_-, R4.Pin_0, R7.Pin_0, U2.3
  N1: DTMF-IC1.GS, R7.Pin_1
  N2: DTMF-IC1.Vref, R3.Pin_0, R4.Pin_1
  GND: DTMF-IC1.INH, DTMF-IC1.PWDn, DTMF-IC1.VSS_(GND), Componente1.GND
  N3: DTMF-IC1.OSC1, XTAL2.pin_1
  N4: DTMF-IC1.OSC2, XTAL2.pin_0
  5V: DTMF-IC1.TOE, DTMF-IC1.Vdd, Componente1.5V, C3.1
  N5: DTMF-IC1.Q1, Componente1.D9_PWM
  N6: DTMF-IC1.Q2, Componente1.D10_PWM/SS
  N7: DTMF-IC1.Q3, Componente1.D11_PWM/MOSI
  N8: DTMF-IC1.Q4, Componente1.D12/MISO
  N9: DTMF-IC1.StD, Componente1.D2
  N10: DTMF-IC1.ESt, R8.Pin_0
  N11: DTMF-IC1.St/GT, R8.Pin_1, C3.0
  N12: R1.Pin_0, D2.anode, R5.Pin_1
  N13: R1.Pin_1, U2.1
  N14: R2.Pin_0, D1.anode, R6.Pin_1
  N15: R2.Pin_1, U2.2
  N16: D1.cathode, D2.cathode
  N17: C1.0, R5.Pin_0
  - controle: C1.1, D3.anode, D4.anode
  N18: C2.0, R6.Pin_0
  + controle: C2.1, D5.cathode, D6.cathode
  + hook: J1.2, D4.cathode, D5.anode
  - hook: J1.6, D3.cathode, D6.anode

notes:
  Workshop Telefonia e Automação, 3.0
