# Fritzing sketch Bina - 4 (saved by Fritzing 0.8.7b)
breadboards: 1

parts:
  R1 = Resistor [tolerance=±5% resistance=56k package=THT]
  R2 = Resistor [tolerance=±5% resistance=56k package=THT]
  R3 = Resistor [tolerance=±5% resistance=47k package=THT]
  R4 = Resistor [tolerance=±5% resistance=68k package=THT]
  D1 = Zener Diode [part_number=1N4732A breakdown_voltage=5.6V package="300 mil [THT]"]
  D2 = Zener Diode [part_number=1N4732A breakdown_voltage=5.6V package="300 mil [THT]"]
  C1 = Ceramic Capacitor [capacitance=100nF voltage=500V package="100 mil [THT, multilayer]"]
  C2 = Ceramic Capacitor [capacitance=100nF voltage=500V package="100 mil [THT, multilayer]"]
  R5 = Resistor [tolerance=±5% resistance=56k package=THT]
  R6 = Resistor [tolerance=±5% resistance=56k package=THT]
  J1 = RJ11 Jack [package=rj11-6]
  R7 = Resistor [tolerance=±5% resistance=150k package=THT]  # not connected
  XTAL2 = Crystal [package=THT]  # not connected
  Componente1 = Arduino Uno (Rev3)
  R8 = Resistor [tolerance=±5% resistance=330k package=THT]  # not connected
  C3 = Ceramic Capacitor [capacitance=100nF package="100 mil [THT, multilayer]"]  # not connected
  D3 = Rectifier Diode [part_number=1N4007 package="300 mil [THT]"]
  D4 = Rectifier Diode [part_number=1N4007 package="300 mil [THT]"]
  D5 = Rectifier Diode [part_number=1N4007 package="300 mil [THT]"]
  D6 = Rectifier Diode [part_number=1N4007 package="300 mil [THT]"]
  U2 = Transformer [package=transformer]

nets:
  N1: R1.Pin_0, D2.anode, R5.Pin_1
  N2: R1.Pin_1, U2.1
  N3: R2.Pin_0, D1.anode, R6.Pin_1
  N4: R2.Pin_1, U2.2
  N5: R3.Pin_1, U2.4
  N6: R4.Pin_0, U2.3
  N7: D1.cathode, D2.cathode
  N8: C1.0, R5.Pin_0
  - controle: C1.1, D3.anode, D4.anode
  N9: C2.0, R6.Pin_0
  + controle: C2.1, D5.cathode, D6.cathode
  + hook: J1.2, D4.cathode, D5.anode
  - hook: J1.6, D3.cathode, D6.anode
  5V: Componente1.5V
  GND: Componente1.GND

notes:
  Workshop Telefonia e Automação, 3.0
