# Fritzing sketch Circuito Base Telefonia - Sinalização e Audio (saved by Fritzing 0.8.7b)
breadboards: 1

parts:
  R7 = Resistor [tolerance=±5% resistance=56k package=THT]
  R8 = Resistor [tolerance=±5% resistance=56k package=THT]
  R9 = Resistor [tolerance=±5% resistance=56k package=THT]
  R10 = Resistor [tolerance=±5% resistance=56k package=THT]
  D7 = Zener Diode [part_number=1N4732A breakdown_voltage=5.6V package="300 mil [THT]"]
  D8 = Zener Diode [part_number=1N4732A breakdown_voltage=5.6V package="300 mil [THT]"]
  C3 = Ceramic Capacitor [capacitance=100nF voltage=500V package="100 mil [THT, multilayer]"]
  C4 = Ceramic Capacitor [capacitance=100nF voltage=500V package="100 mil [THT, multilayer]"]
  J2 = RJ11 Jack [package=rj11-6]
  U3 = Transformer [package=transformer]
  D9 = Rectifier Diode [part_number=1N4007 package="300 mil [THT]"]
  D10 = Rectifier Diode [part_number=1N4007 package="300 mil [THT]"]
  D11 = Rectifier Diode [part_number=1N4007 package="300 mil [THT]"]
  D12 = Rectifier Diode [part_number=1N4007 package="300 mil [THT]"]

nets:
  N1: R7.Pin_0, C3.0
  N2: R7.Pin_1, R9.Pin_0, D8.anode
  N3: R8.Pin_0, C4.0
  N4: R8.Pin_1, R10.Pin_0, D7.anode
  N5: R9.Pin_1, U3.2
  N6: R10.Pin_1, U3.1
  N7: D7.cathode, D8.cathode
  + controle: C3.1, D9.cathode, D10.cathode
  - controle: C4.1, D11.anode, D12.anode
  + hook: J2.2, D10.anode, D11.cathode
  - hook: J2.6, D9.anode, D12.cathode
  - audio: U3.3
  + audio: U3.4
