# Fritzing sketch Circuito Base Telefonia - Sinalização, Audio e Alimentação (saved by Fritzing 0.8.7b)
breadboards: 1

parts:
  R7 = Resistor [tolerance=±5% resistance=56k package=THT]
  R8 = Resistor [tolerance=±5% resistance=56k package=THT]
  R9 = Resistor [tolerance=±5% resistance=56k package=THT]
  R10 = Resistor [tolerance=±5% resistance=56k package=THT]
  D7 = Zener Diode [part_number=1N4742A breakdown_voltage=12V package="300 mil [THT]"]
  C3 = Ceramic Capacitor [capacitance=100nF voltage=500V package="100 mil [THT, multilayer]"]
  C4 = Ceramic Capacitor [capacitance=100nF voltage=500V package="100 mil [THT, multilayer]"]
  J2 = RJ11 Jack [package=rj11-6]
  U3 = Transformer [package=transformer]
  D9 = Rectifier Diode [part_number=1N4007 package="300 mil [THT]"]
  D10 = Rectifier Diode [part_number=1N4007 package="300 mil [THT]"]
  D11 = Rectifier Diode [part_number=1N4007 package="300 mil [THT]"]
  D12 = Rectifier Diode [part_number=1N4007 package="300 mil [THT]"]
  D13 = Zener Diode [part_number=1N4734A breakdown_voltage=5.1V package="Melf DO-213 AB [SMD]"]
  C5 = Ceramic Capacitor [capacitance=100nF voltage=50V package="100 mil [THT, multilayer]"]
  R11 = Resistor [tolerance=±5% resistance=200k package=THT]
  C6 = Ceramic Capacitor [capacitance=100nF package="100 mil [THT, multilayer]"]
  R12 = Resistor [tolerance=±5% resistance=10k package=THT]
  D14 = Zener Diode [part_number=1N4747A breakdown_voltage=20V package="Melf DO-213 AB [SMD]"]
  U4 = Optocoupler [package=THT]
  R13 = Resistor [tolerance=±5% resistance=10k package=THT]
  R28 = Resistor [tolerance=±5% resistance=10k package=THT]
  R29 = Resistor [tolerance=±5% resistance=10k package=THT]
  U10 = Optocoupler [package=THT]
  U11 = Optocoupler [package=THT]
  Q5 = NPN-Transistor [part_number=2n3904 package="TO92 [THT]"]
  Q6 = NPN-Transistor [part_number=2n3904 package="TO92 [THT]"]
  R30 = Resistor [tolerance=±5% resistance=33k package=THT]
  R31 = Resistor [tolerance=±5% resistance=4.7k package=THT]
  R32 = Resistor [tolerance=±5% resistance=3.3k package=THT]
  R33 = Resistor [tolerance=±5% resistance=56k package=THT]
  R34 = Resistor [tolerance=±5% resistance=22k package=THT]

nets:
  N1: R7.Pin_0, C3.0
  N2: R7.Pin_1, R9.Pin_0, D7.cathode
  N3: R8.Pin_0, C4.0
  N4: R8.Pin_1, R10.Pin_0, D7.anode
  N5: R9.Pin_1, U3.2
  N6: R10.Pin_1, U3.1
  + controle: C3.1, D9.cathode, D10.cathode, R11.Pin_0, C6.1, R30.Pin_1, R32.Pin_1, R33.Pin_1
  - controle/Vss: C4.1, D11.anode, D12.anode, D13.anode, C5.1, R12.Pin_0, Q5.E, Q6.E, R31.Pin_0
  + hook: J2.2, D10.anode, D11.cathode
  - hook: J2.6, D9.anode, D12.cathode
  - audio: U3.3
  + audio: U3.4
  Vcc: D13.cathode, C5.0, R11.Pin_1
  N7: C6.0, D14.cathode
  N8: R12.Pin_1, U4.Pin_2
  N9: D14.anode, U4.Pin_1
  GND: U4.Pin_4, U10.Pin_4, U11.Pin_4
  TTL Ring Signal: U4.Pin_5, R13.Pin_0
  5V: R13.Pin_1, R28.Pin_1, R29.Pin_1
  TTL Off-Hook Signal: R28.Pin_0, U11.Pin_5
  TTL On-Hook Signal: R29.Pin_0, U10.Pin_5
  N10: U10.Pin_1, R30.Pin_0
  N11: U10.Pin_2, Q5.C, R34.Pin_0
  N12: U11.Pin_1, R32.Pin_0
  N13: U11.Pin_2, Q6.C
  N14: Q5.B, R31.Pin_1, R33.Pin_0
  N15: Q6.B, R34.Pin_1

notes:
  Entre VSS e VCC deverá se obter 5V de tensão
  Circuito para Obtenção de Tensão
  Se a Linha Tocaro sinal passa pelo filtro e attera o pino.
  Saida acoplada com filtro e transformador de 600ohms para conexão com setor de audio
  Saída para uso na sinalização e obtenção de tensões.
  Saída para controle de atendimento
  Circuito para Obtenção do estado da linha
