# Fritzing sketch Circuito Base Telefonia - Sinalização (saved by Fritzing 0.8.7b)
breadboards: 1

parts:
  R21 = Resistor [tolerance=±5% resistance=10k package=THT]
  R22 = Resistor [tolerance=±5% resistance=10k package=THT]
  U8 = Optocoupler [package=THT]
  U9 = Optocoupler [package=THT]
  Q3 = NPN-Transistor [part_number=2n3904 package="TO92 [THT]"]
  Q4 = NPN-Transistor [part_number=2n3904 package="TO92 [THT]"]
  R23 = Resistor [tolerance=±5% resistance=33k package=THT]
  R24 = Resistor [tolerance=±5% resistance=4.7k package=THT]
  R25 = Resistor [tolerance=±5% resistance=3.3k package=THT]
  R26 = Resistor [tolerance=±5% resistance=56k package=THT]
  R27 = Resistor [tolerance=±5% resistance=22k package=THT]

nets:
  TTL Off-Hook Signal: R21.Pin_0, U9.Pin_5
  5V: R21.Pin_1, R22.Pin_1
  TTL On-Hook Signal: R22.Pin_0, U8.Pin_5
  N1: U8.Pin_1, R23.Pin_0
  N2: U8.Pin_2, Q3.C, R27.Pin_0
  GND: U8.Pin_4, U9.Pin_4
  N3: U9.Pin_1, R25.Pin_0
  N4: U9.Pin_2, Q4.C
  - controle: Q3.E, Q4.E, R24.Pin_0
  N5: Q3.B, R24.Pin_1, R26.Pin_0
  N6: Q4.B, R27.Pin_1
  + controle: R23.Pin_1, R25.Pin_1, R26.Pin_1

notes:
  Circuito para Obtenção do estado da linha
